# Fritzing sketch ESP DHT (saved by Fritzing 0.9.3b)
circuit board: 8.46667cm x 5.64444cm
perfboards: 1

parts:
  ESP1 = ESP8266 WiFi Module [part_number=ESP8266]
  LED_Out3 = female pin header, 4 pins [form="♀ (female)"]
  LED_Out4 = female pin header, 4 pins [form="♀ (female)"]
  U3 = Voltage Regulator -- 3.3 V -- LM1117
  Part2 = Adafruit Micro USB Breakout [part_number="Adafruit #1833"]
  DHT2 = DHT22 Humidity and Temperature Sensor
  R5 = Resistor [tolerance=±5% resistance=10k package="0603 [SMD]"]

nets:
  N1: ESP1.RXD, LED_Out3.pin4
  VCC: ESP1.VCC, ESP1.GPIO_0, ESP1.RST, ESP1.CH_PD, LED_Out3.pin3, LED_Out4.pin2, LED_Out4.pin3, LED_Out4.pin4, U3.OUT, DHT2.VDD, R5.Pin_1
  N2: ESP1.GPIO_2, LED_Out3.pin2, DHT2.DATA, R5.Pin_0
  GND: ESP1.GND, LED_Out3.pin1, U3.GND, Part2.GND, DHT2.GND
  N3: ESP1.TXD, LED_Out4.pin1
  N4: U3.IN, Part2.VBUS

custom parts:
  ESP8266 WiFi Module: Generic WiFi Module based on the ESP8266 with onboard PCB antenna and UART communications
  Voltage Regulator -- 3.3 V -- LM1117: LM1117-3.3 Voltage regulator, 3.3 V output. Note that the pinout order is not the same as LM7805 or LM7833.
  Adafruit Micro USB Breakout: Simple but effective - this breakout board has a USB Micro-B connector, with all 5 pins broken out. Great for pairing with a microcontroller with USB support, or adding USB 5V power to a project. We use a micro-AB connector with through-hole shielding pads for an excellent strong connection - it won't rip off by accident! Comes with one fully assembled and tested micro B breakout PCB and a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
